# Fritzing sketch Platine (saved by Fritzing 0.9.3b)
breadboards: 1

parts:
  Raspberry_Pi_1 = Raspberry Pi 3 [part_number=RPI-3-V1.2]
  J1 = Basic Servo
  LED1 = RGB LED (com. cathode, rgb) [package="5 mm [THT]"]
  R1 = Resistor [tolerance=±5% resistance=220 package=THT]
  S1 = Pushbutton [package="[THT]"]
  R2 = Resistor [tolerance=±5% resistance=220 package=THT]
  U1 = mystery part, 3 pins [chip_label=Speaker]

nets:
  N1: Raspberry_Pi_1.GPIO17, J1.pulse
  N2: Raspberry_Pi_1.GPIO22, LED1.red_anode
  GND: Raspberry_Pi_1.GND, J1.gnd, R1.Pin_1, R2.Pin_0, U1.pin1
  N3: Raspberry_Pi_1.GPIO21, S1.Pin_3, S1.Pin_4, R2.Pin_1
  N4: Raspberry_Pi_1.GPIO20, U1.pin2
  N5: Raspberry_Pi_1.GPIO24, LED1.blue_anode
  N6: Raspberry_Pi_1.GPIO23, LED1.green_anode
  5V: Raspberry_Pi_1.5V, J1.vcc, S1.Pin_1, S1.Pin_2, U1.pin3
  N7: LED1.common_cathode, R1.Pin_0
