# Fritzing sketch Schaltplan (saved by Fritzing 0.9.3b)
breadboards: 1

parts:
  Raspberry_Pi_1 = Raspberry Pi 3 [part_number=RPI-3-V1.2]
  Servo = Basic Servo
  LED1 = RGB LED (com. cathode, rgb) [package="5 mm [THT]"]
  Tür = Pushbutton [package="[THT]"]
  R2 = Resistor [tolerance=±5% resistance=220 package=THT]
  Buzzer = Piezo Speaker
  Knopf = Pushbutton [package="[THT]"]
  R3 = Resistor [tolerance=±5% resistance=220 package=THT]
  Lüfter = DC Motor

nets:
  N1: Raspberry_Pi_1.GPIO2, LED1.red_anode
  N2: Raspberry_Pi_1.GPIO3, LED1.green_anode
  N3: Raspberry_Pi_1.GPIO4, LED1.blue_anode
  GND: Raspberry_Pi_1.GND, Servo.gnd, LED1.common_cathode, R2.Pin_0, Buzzer.pin1, R3.Pin_1, Lüfter.pin_1
  N4: Raspberry_Pi_1.GPIO17, Buzzer.pin2
  N5: Raspberry_Pi_1.GPIO27, Servo.pulse
  N6: Raspberry_Pi_1.GPIO19, Tür.Pin_3, Tür.Pin_4, R2.Pin_1
  N7: Raspberry_Pi_1.GPIO26, Knopf.Pin_1, Knopf.Pin_2, R3.Pin_0
  5V: Raspberry_Pi_1.5V, Servo.vcc, Tür.Pin_1, Tür.Pin_2, Knopf.Pin_3, Lüfter.pin_2
